# Fritzing sketch pump Sketch (saved by Fritzing 1.0.0rc)
breadboards: 1

parts:
  WATER_PUMP_12v = water pump/motor
  Part2 = Adafruit Feather ESP32-S2 [part_number="Adafruit #5000"]
  Relay = RELAY [package=relay-jzc]
  12_V_Power_Supply = 2.1mm Barrel Jack with Terminal Block
  R4 = Resistor [tolerance=±5% power=0.25 resistance=10k package=THT]
  Liquid_Level_Sensor_Switch = Reed switch [package=THT]  # not connected
  R5 = Resistor [tolerance=±5% power=0.25 resistance=1k package=THT]
  Liquid_Level_Sensor_Switch_2 = Reed switch [package=THT]  # not connected
  R6 = Resistor [tolerance=±5% power=0.25 resistance=10k package=THT]
  R7 = Resistor [tolerance=±5% power=0.25 resistance=1k package=THT]
  12V_to_5V_converter = RioRand LM2596

nets:
  N1: WATER_PUMP_12v.pin_1, Part2.GND, Part2.A2, Relay.NO, 12_V_Power_Supply.NEG, R5.Pin_1, R7.Pin_1, 12V_to_5V_converter.Pin_1, 12V_to_5V_converter.Pin_4
  N2: WATER_PUMP_12v.pin_2, Relay.COIL1
  N3: Part2.A1, R6.Pin_1
  N4: Part2.A0, R4.Pin_1
  N5: Part2.VBUS, Relay.COIL2, 12V_to_5V_converter.Pin_3
  N6: Part2.D5, Relay.NC
  N7: Relay.MAIN, 12_V_Power_Supply.POS, 12V_to_5V_converter.Pin_2

custom parts:
  water pump/motor: WATER PUMP BY ARDUBLOCKTR
  Adafruit Feather ESP32-S2: What's Feather-shaped and has an ESP32-S2 WiFi module? What has a STEMMA QT connector for I2C devices and a built in ambient sensor? What has your favorite Espressif WiFi microcontroller and lots of Flash and RAM memory for your next IoT project? What will make your next IoT project sensor project flyyyyy? That's right - it's the new Adafruit ESP32-S2 Feather and Adafruit ESP32-S2 Feather with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
